// Logisim project MIPS.circ as structural Verilog: 2 circuits, main circuit Init Check
module Init_Check (
  input  A0,
  input  A1,
  input  A2,
  input  A3,
  input  A4,
  input  A5,
  input  A6,
  input  A7,
  input  A8,
  input  A9,
  input  A10,
  input  A11,
  input  A12,
  input  A13,
  input  A14,
  input  A15,
  input  A16,
  input  A17,
  input  A18,
  input  A19,
  input  A20,
  input  A21,
  input  A22,
  input  A23,
  input  A24,
  input  A25,
  input  A26,
  input  A27,
  input  A28,
  input  A29,
  input  A30,
  input  A31,
  output out_33
);

  wire and_1_out, and_2_out, and_3_out, and_4_out, and_5_out, and_6_out, and_7_out, and_8_out, and_9_out,
       and_10_out, and_11_out, and_12_out, and_13_out, and_14_out, and_15_out, and_16_out, and_17_out,
       and_18_out, and_19_out, and_20_out, and_21_out, and_22_out, and_23_out, and_24_out, and_25_out,
       and_26_out, and_27_out, and_28_out, and_29_out, and_30_out;

  and and_1 (and_1_out, A0, A1);
  and and_2 (and_2_out, A2, A3);
  and and_3 (and_3_out, A4, A5);
  and and_4 (and_4_out, A6, A7);
  and and_5 (and_5_out, A8, A9);
  and and_6 (and_6_out, A10, A11);
  and and_7 (and_7_out, A12, A13);
  and and_8 (and_8_out, A14, A15);
  and and_9 (and_9_out, A16, A17);
  and and_10 (and_10_out, A18, A19);
  and and_11 (and_11_out, A20, A21);
  and and_12 (and_12_out, A22, A23);
  and and_13 (and_13_out, A24, A25);
  and and_14 (and_14_out, A26, A27);
  and and_15 (and_15_out, A28, A29);
  and and_16 (and_16_out, A30, A31);
  and and_17 (and_17_out, and_1_out, and_2_out);
  and and_18 (and_18_out, and_3_out, and_4_out);
  and and_19 (and_19_out, and_5_out, and_6_out);
  and and_20 (and_20_out, and_7_out, and_8_out);
  and and_21 (and_21_out, and_9_out, and_10_out);
  and and_22 (and_22_out, and_11_out, and_12_out);
  and and_23 (and_23_out, and_13_out, and_14_out);
  and and_24 (and_24_out, and_15_out, and_16_out);
  and and_25 (and_25_out, and_17_out, and_18_out);
  and and_26 (and_26_out, and_25_out, and_27_out);
  and and_27 (and_27_out, and_19_out, and_20_out);
  and and_28 (and_28_out, and_21_out, and_22_out);
  and and_29 (and_29_out, and_28_out, and_30_out);
  and and_30 (and_30_out, and_23_out, and_24_out);
  and and_31 (out_33, and_26_out, and_29_out);
endmodule

module syscall_noop (
  input  A0,
  input  A1,
  input  A2,
  input  A3,
  input  A4,
  input  A5,
  input  A6,
  input  A7,
  input  A8,
  input  A9,
  input  A10,
  input  A11,
  input  A12,
  input  A13,
  input  A14,
  input  A15,
  input  A16,
  input  A17,
  input  A18,
  input  A19,
  input  A20,
  input  A21,
  input  A22,
  input  A23,
  input  A24,
  input  A25,
  input  A26,
  input  A27,
  input  A28,
  input  A29,
  input  A30,
  input  A31,
  output out_33
);

  wire and_1_out, and_2_out, and_3_out, and_4_out, and_5_out, and_6_out, and_7_out, and_8_out, and_9_out,
       and_10_out, and_11_out, and_12_out, and_13_out, and_14_out, and_15_out, and_16_out, and_17_out,
       and_18_out, and_19_out, and_20_out, and_21_out, and_22_out, and_23_out, and_24_out, and_25_out,
       and_26_out, and_27_out, and_28_out, and_29_out, and_30_out, not_1_out, not_2_out, not_3_out,
       not_4_out, not_5_out, not_6_out, not_7_out, not_8_out, not_9_out, not_10_out, not_11_out, not_12_out,
       not_13_out, not_14_out, not_15_out, not_16_out, not_17_out, not_18_out, not_19_out, not_20_out,
       not_21_out, not_22_out, not_23_out, not_24_out, not_25_out, not_26_out, not_27_out, not_28_out,
       not_29_out, not_30_out, not_31_out, not_32_out;

  not not_1 (not_1_out, A0);
  not not_2 (not_2_out, A1);
  not not_3 (not_3_out, A2);
  not not_4 (not_4_out, A3);
  not not_5 (not_5_out, A4);
  not not_6 (not_6_out, A5);
  not not_7 (not_7_out, A6);
  not not_8 (not_8_out, A7);
  not not_9 (not_9_out, A8);
  not not_10 (not_10_out, A9);
  not not_11 (not_11_out, A10);
  not not_12 (not_12_out, A11);
  not not_13 (not_13_out, A12);
  not not_14 (not_14_out, A13);
  not not_15 (not_15_out, A14);
  not not_16 (not_16_out, A15);
  not not_17 (not_17_out, A16);
  not not_18 (not_18_out, A17);
  not not_19 (not_19_out, A18);
  not not_20 (not_20_out, A19);
  not not_21 (not_21_out, A20);
  not not_22 (not_22_out, A21);
  not not_23 (not_23_out, A22);
  not not_24 (not_24_out, A23);
  not not_25 (not_25_out, A24);
  not not_26 (not_26_out, A25);
  not not_27 (not_27_out, A26);
  not not_28 (not_28_out, A27);
  not not_29 (not_29_out, A28);
  not not_30 (not_30_out, A29);
  not not_31 (not_31_out, A30);
  not not_32 (not_32_out, A31);
  and and_1 (and_1_out, not_1_out, not_2_out);
  and and_2 (and_2_out, not_3_out, not_4_out);
  and and_3 (and_3_out, and_2_out, and_4_out);
  and and_4 (and_4_out, not_5_out, not_6_out);
  and and_5 (and_5_out, not_7_out, not_8_out);
  and and_6 (and_6_out, and_5_out, and_7_out);
  and and_7 (and_7_out, not_9_out, not_10_out);
  and and_8 (and_8_out, not_11_out, not_12_out);
  and and_9 (and_9_out, and_8_out, and_10_out);
  and and_10 (and_10_out, not_13_out, not_14_out);
  and and_11 (and_11_out, not_15_out, not_16_out);
  and and_12 (and_12_out, and_11_out, and_13_out);
  and and_13 (and_13_out, not_17_out, not_18_out);
  and and_14 (and_14_out, not_19_out, not_20_out);
  and and_15 (and_15_out, and_14_out, and_16_out);
  and and_16 (and_16_out, not_21_out, not_22_out);
  and and_17 (and_17_out, not_23_out, not_24_out);
  and and_18 (and_18_out, and_17_out, and_19_out);
  and and_19 (and_19_out, not_25_out, not_26_out);
  and and_20 (and_20_out, not_27_out, not_28_out);
  and and_21 (and_21_out, and_20_out, and_22_out);
  and and_22 (and_22_out, not_29_out, not_30_out);
  and and_23 (and_23_out, not_31_out, not_32_out);
  and and_24 (and_24_out, and_1_out, and_3_out);
  and and_25 (and_25_out, and_9_out, and_12_out);
  and and_26 (and_26_out, and_15_out, and_18_out);
  and and_27 (and_27_out, and_21_out, and_23_out);
  and and_28 (and_28_out, and_6_out, and_25_out);
  and and_29 (and_29_out, and_28_out, and_30_out);
  and and_30 (and_30_out, and_26_out, and_27_out);
  or or_1 (out_33, and_24_out, and_29_out);
endmodule
